# Fritzing sketch circuitDiagram (saved by Fritzing 0.6.3b)
breadboards: 1

parts:
  Arduino2 = Arduino
  J1 = Basic Servo

nets:
  N1: Arduino2.D9, J1.pulse
  +5V: Arduino2.+5V, J1.vcc
  GND: Arduino2.GND, J1.gnd

notes:
  In this example, potentiometer values are read in through an 'Analog In' pin. The values are then used to control the position of a servo motor. Related examples: http://arduino.cc/en/Tutorial/AnalogInput http://arduino.cc/en/Tutorial/Knob
